// Logisim project Labo_05_Biefer_Cortes.circ as structural Verilog: 7 circuits, main circuit registreDecalage_4bits
module registreDecalage_4bits (
  input  R,
  input  L,
  input  [3:0] D,
  input  [1:0] S,
  input  clk,
  output [3:0] Q
);

  wire multiplexer_1_out, multiplexer_2_out, multiplexer_3_out, multiplexer_4_out;

  Multiplexer #(.select(2), .enable("false")) multiplexer_1 (
    .in0(Q[3]), .in1(D[3]), .in2(Q[2]), .in3(L), .out(multiplexer_1_out), .sel(S));
  D_Flip_Flop d_ff_1 (.D(multiplexer_1_out), .clk(clk), .Q(Q[3]));  // open: Qn, preset, reset
  Multiplexer #(.select(2), .enable("false")) multiplexer_2 (
    .in0(Q[2]), .in1(D[2]), .in2(Q[1]), .in3(Q[3]), .out(multiplexer_2_out), .sel(S));
  D_Flip_Flop d_ff_2 (.D(multiplexer_2_out), .clk(clk), .Q(Q[2]));  // open: Qn, preset, reset
  Multiplexer #(.select(2), .enable("false")) multiplexer_3 (
    .in0(Q[1]), .in1(D[1]), .in2(Q[0]), .in3(Q[2]), .out(multiplexer_3_out), .sel(S));
  D_Flip_Flop d_ff_3 (.D(multiplexer_3_out), .clk(clk), .Q(Q[1]));  // open: Qn, preset, reset
  Multiplexer #(.select(2), .enable("false")) multiplexer_4 (
    .in0(Q[0]), .in1(D[0]), .in2(R), .in3(Q[1]), .out(multiplexer_4_out), .sel(S));
  D_Flip_Flop d_ff_4 (.D(multiplexer_4_out), .clk(clk), .Q(Q[0]));  // open: Qn, preset, reset

  // Notes on the sheet:
  //   Attention, votre version de Logisim
  //   ne contient pas de tracker. Si vous
  //   enregistrez votre projet, toutes les
  //   informations du tracker seront
  //   définitivement effacées.
endmodule

module registreDecalage_8bits (
  input  R,
  input  L,
  input  [7:0] D,
  input  [1:0] S,
  input  clk,
  output [7:0] Q
);

  registreDecalage_4bits weak_bits (.R(R), .L(Q[4]), .D(D[3:0]), .S(S), .clk(clk), .Q(Q[3:0]));
  registreDecalage_4bits strong_bits (.R(Q[3]), .L(L), .D(D[7:4]), .S(S), .clk(clk), .Q(Q[7:4]));

  // Notes on the sheet:
  //   Attention, votre version de Logisim
  //   ne contient pas de tracker. Si vous
  //   enregistrez votre projet, toutes les
  //   informations du tracker seront
  //   définitivement effacées.
endmodule

module registreLFSR_8bits (
  input  clk,
  output [7:0] Q
);

  wire xnor_1_out, xnor_2_out, xnor_3_out;

  xnor xnor_1 (xnor_1_out, Q[7], xnor_2_out);
  registreDecalage_8bits registredecalage_8bits_1 (
    .R(1'b0), .L(xnor_1_out), .D({8{1'b0}}), .S(2'b11), .clk(clk), .Q(Q));
  xnor xnor_2 (xnor_2_out, Q[5], xnor_3_out);
  xnor xnor_3 (xnor_3_out, Q[3], Q[2]);

  // Notes on the sheet:
  //   Attention, votre version de Logisim
  //   ne contient pas de tracker. Si vous
  //   enregistrez votre projet, toutes les
  //   informations du tracker seront
  //   définitivement effacées.
endmodule

module affichageRegistre (
);

  wire clock_1_out;
  wire [7:0] registrelfsr_8bits_1_q;

  Clock clock_1 (.out(clock_1_out));
  Hex_Digit_Display hex_digit_display_1 (.value(registrelfsr_8bits_1_q[7:4]));  // open: dp
  registreLFSR_8bits registrelfsr_8bits_1 (.clk(clock_1_out), .Q(registrelfsr_8bits_1_q));
  Hex_Digit_Display hex_digit_display_2 (.value(registrelfsr_8bits_1_q[3:0]));  // open: dp

  // Notes on the sheet:
  //   Attention, votre version de Logisim
  //   ne contient pas de tracker. Si vous
  //   enregistrez votre projet, toutes les
  //   informations du tracker seront
  //   définitivement effacées.
endmodule

module recepteur_8bits (
  input  b,
  input  reset,
  output [7:0] affichage
);

  wire and_1_out, and_2_out, and_3_out, and_4_out, and_5_out, clk_out, compteur3_c3, compteur7_c7,
       nand_1_out, not_1_out, not_2_out, not_3_out, or_1_out, or_2_out, Q0_q, Q1_q, Q2_q;
  wire [1:1] and_6_out;
  wire [7:0] SHR_q;

  Clock clk (.out(clk_out));
  not not_1 (not_1_out, reset);
  and and_1 (and_1_out, compteur3_c3, Q1_q);
  not not_2 (not_2_out, Q1_q);
  nand nand_1 (nand_1_out, compteur3_c3, compteur7_c7);
  and and_2 (and_2_out, Q1_q, nand_1_out);
  not not_3 (not_3_out, b);
  and and_3 (and_3_out, Q0_q, b);
  compteur_0a3 compteur3 (.Enable(1'b1), .clk(clk_out), .reset(not_2_out), .c3(compteur3_c3));
  compteur_0a7 compteur7 (.enable(and_1_out), .clk(clk_out), .reset(not_2_out), .c7(compteur7_c7));
  and and_4 (and_4_out, compteur7_c7, compteur3_c3, Q1_q);
  and and_5 (and_5_out, not_3_out, Q0_q);
  and and_6 (and_6_out[1], Q1_q, compteur3_c3);
  D_Flip_Flop Q2 (.D(and_4_out), .clk(clk_out), .Q(Q2_q), .reset(not_1_out));  // open: Qn, preset
  D_Flip_Flop Q1 (.D(or_1_out), .clk(clk_out), .Q(Q1_q), .reset(not_1_out));  // open: Qn, preset
  or or_1 (or_1_out, and_2_out, and_5_out);
  D_Flip_Flop Q0 (.D(or_2_out), .clk(clk_out), .Q(Q0_q), .preset(not_1_out));  // open: Qn, reset
  or or_2 (or_2_out, and_3_out, Q2_q);
  Register registreSortie (.D(SHR_q), .en(Q2_q), .clk(clk_out), .Q(affichage), .clr(Q1_q));
  registreDecalage_8bits SHR (.R(1'b0), .L(b), .D({8{1'b0}}), .S({2{and_6_out[1]}}), .clk(clk_out), .Q(SHR_q));

  // Notes on the sheet:
  //   Attention, votre version de Logisim
  //   ne contient pas de tracker. Si vous
  //   enregistrez votre projet, toutes les
  //   informations du tracker seront
  //   définitivement effacées.
endmodule

module compteur_0a3 (
  input  Enable,
  input  clk,
  input  reset,
  output c3
);

  wire and_1_out, d_ff_1_q, d_ff_2_q, xor_1_out, xor_2_out;

  xor xor_1 (xor_1_out, d_ff_1_q, Enable);
  and and_1 (and_1_out, d_ff_1_q, Enable);
  xor xor_2 (xor_2_out, d_ff_2_q, and_1_out);
  // AND_Gate and_2 has open pins: in0=d_ff_2_q, in1=and_1_out, out=open
  D_Flip_Flop d_ff_1 (.D(xor_1_out), .clk(clk), .Q(d_ff_1_q), .reset(reset));  // open: Qn, preset
  D_Flip_Flop d_ff_2 (.D(xor_2_out), .clk(clk), .Q(d_ff_2_q), .reset(reset));  // open: Qn, preset
  and and_3 (c3, d_ff_1_q, d_ff_2_q);

  // Notes on the sheet:
  //   Attention, votre version de Logisim
  //   ne contient pas de tracker. Si vous
  //   enregistrez votre projet, toutes les
  //   informations du tracker seront
  //   définitivement effacées.
endmodule

module compteur_0a7 (
  input  enable,
  input  clk,
  input  reset,
  output c7
);

  wire and_1_out, and_2_out, d_ff_1_q, d_ff_2_q, d_ff_3_q, xor_1_out, xor_2_out, xor_3_out;

  and and_1 (and_1_out, d_ff_1_q, enable);
  and and_2 (and_2_out, d_ff_2_q, and_1_out);
  // AND_Gate and_3 has open pins: in0=d_ff_3_q, in1=and_2_out, out=open
  D_Flip_Flop d_ff_1 (.D(xor_1_out), .clk(clk), .Q(d_ff_1_q), .reset(reset));  // open: Qn, preset
  xor xor_1 (xor_1_out, d_ff_1_q, enable);
  D_Flip_Flop d_ff_2 (.D(xor_2_out), .clk(clk), .Q(d_ff_2_q), .reset(reset));  // open: Qn, preset
  xor xor_2 (xor_2_out, d_ff_2_q, and_1_out);
  D_Flip_Flop d_ff_3 (.D(xor_3_out), .clk(clk), .Q(d_ff_3_q), .reset(reset));  // open: Qn, preset
  xor xor_3 (xor_3_out, d_ff_3_q, and_2_out);
  and and_4 (c7, d_ff_1_q, d_ff_2_q, d_ff_3_q);

  // Notes on the sheet:
  //   Attention, votre version de Logisim
  //   ne contient pas de tracker. Si vous
  //   enregistrez votre projet, toutes les
  //   informations du tracker seront
  //   définitivement effacées.
endmodule
